# Fritzing sketch schematics (saved by Fritzing 1.0.3b)
circuit board: 4.79304cm x 4.76977cm

parts:
  Nano = Arduino Nano (Rev3.0)
  M1 = ph-4502c_1
  J1 = Dagu DGServo 9g header (male) [package=THT]

nets (from the schematic view):
  N1: Nano.GND, M1.connector4
  N2: Nano.VIN, M1.connector5
  N3: Nano.A5, J1.Vcc
  N4: Nano.A4, J1.pulse
  N5: Nano.A1, M1.connector0
  N6: Nano.A0, M1.connector2, M1.connector3

notes:
  I2C data
  I2C clock
